// Digital circuit addition.dig as structural Verilog
module addition (
  input  [1:0] inA,
  input  [1:0] inB,
  input  inC,
  input  inC_2,
  input  outC_2,
  output [1:0] outS,
  output outC
);

  wire fulladder_1_outc, fulladder_2_outc, multiplexer_1_out;

  Multiplexer multiplexer_1 (.sel(inC_2), .in_0(1'b0), .in_1(inC), .out(multiplexer_1_out));
  fulladder fulladder_1 (.inA(inA[0]), .inB(inB[0]), .inC(multiplexer_1_out), .outS(outS[0]), .outC(fulladder_1_outc));
  fulladder fulladder_2 (.inA(inA[1]), .inB(inB[1]), .inC(fulladder_1_outc), .outS(outS[1]), .outC(fulladder_2_outc));
  Multiplexer multiplexer_2 (.sel(outC_2), .in_0(inC), .in_1(fulladder_2_outc), .out(outC));

  // Other names for the same wires on the sheet: tunnel1 = inC
endmodule
