// Digital circuit fulladder.dig as structural Verilog
module fulladder (
  input  inA,
  input  inB,
  input  inC,
  output outS,
  output outC
);

  wire and_1_out, and_2_out, xor_1_out;

  xor xor_1 (xor_1_out, inA, inB);
  and and_1 (and_1_out, xor_1_out, inC);
  and and_2 (and_2_out, inA, inB);
  xor xor_2 (outS, xor_1_out, inC);
  or or_1 (outC, and_1_out, and_2_out);
endmodule
