// Digital circuit halfadder.dig as structural Verilog
module halfadder (
  input  inA,
  input  inB,
  output outS,
  output outC
);

  xor xor_1 (outS, inA, inB);
  and and_1 (outC, inA, inB);
endmodule
