// Digital circuit nand-gate.dig as structural Verilog
module nand_gate (
);

  wire dipswitch_1_out, dipswitch_2_out, nand_1_out, nfet_1_s, pfet_1_d, pfet_3_d;

  DipSwitch dipswitch_1 (.out(dipswitch_1_out));
  DipSwitch dipswitch_2 (.out(dipswitch_2_out));
  // NAnd nand_1 has open pins: In_1=open, In_2=open, out=nand_1_out
  // Not not_1 has open pins: in=nand_1_out, out=open
  PFET pfet_1 (.G(dipswitch_1_out), .S(1'b1), .D(pfet_1_d));
  PFET pfet_2 (.G(dipswitch_2_out), .S(1'b1), .D(pfet_1_d));
  NFET nfet_1 (.G(dipswitch_1_out), .D(pfet_1_d), .S(nfet_1_s));
  NFET nfet_2 (.G(dipswitch_2_out), .D(nfet_1_s), .S(1'b0));
  // And and_1 is placed but not wired
  PFET pfet_3 (.G(pfet_1_d), .S(1'b1), .D(pfet_3_d));
  NFET nfet_3 (.G(pfet_1_d), .D(pfet_3_d), .S(1'b0));
  LED led_1 (.in(pfet_3_d));
endmodule
