// Digital circuit D-latch.dig as structural Verilog
module D_latch (
  input  clk,
  output Q,
  output Qbar
);

  wire and_1_out, Data_out, nand_1_out, nand_2_out, WriteEnable_out;

  DipSwitch Clock ();  // open: out
  DipSwitch WriteEnable (.out(WriteEnable_out));
  LED led_1 (.in(clk));
  DipSwitch Data (.out(Data_out));
  and and_1 (and_1_out, WriteEnable_out, clk);
  Register #(.Bits(8)) register_1 ();  // open: D, C, en, Q
  nand nand_1 (nand_1_out, Data_out, and_1_out);
  nand nand_2 (nand_2_out, nand_1_out, and_1_out);
  nand nand_3 (Q, nand_1_out, Qbar);
  nand nand_4 (Qbar, Q, nand_2_out);
endmodule
