// Digital circuit SR-latch.dig as structural Verilog
module SR_latch (
  output Q,
  output Qbar
);

  wire not_1_out, not_2_out, R_out, S_out;

  DipSwitch S (.out(S_out));
  DipSwitch R (.out(R_out));
  not not_1 (not_1_out, S_out);
  not not_2 (not_2_out, R_out);
  nand nand_1 (Q, not_1_out, Qbar);
  nand nand_2 (Qbar, Q, not_2_out);
endmodule
