// Digital circuit multiplexer2.dig as structural Verilog
module multiplexer2 (
  input  Select,
  input  Input1,
  input  Input0,
  output Output
);

  wire and_1_out, and_2_out, not_1_out, not_2_out;

  not not_1 (not_1_out, Select);
  not not_2 (not_2_out, not_1_out);
  and and_1 (and_1_out, not_2_out, Input1);
  and and_2 (and_2_out, not_1_out, Input0);
  or or_1 (Output, and_1_out, and_2_out);
endmodule
